// Logisim project seq_circuit.circ as structural Verilog: 1 circuit, main circuit main
module main (
  input  in_1,
  input  in_2,
  input  in_3,
  output out_4,
  output out_5
);

  wire and_1_out, and_2_out, nand_1_out, nand_3_out, nand_4_out, not_1_out, or_1_out, xor_1_out;

  xor xor_1 (xor_1_out, in_1, in_2);
  and and_1 (and_1_out, in_1, in_2);
  xor xor_2 (out_4, xor_1_out, nand_1_out);
  nand nand_1 (nand_1_out, nand_3_out, out_5);
  nand nand_2 (out_5, nand_1_out, nand_4_out);
  and and_2 (and_2_out, xor_1_out, nand_1_out);
  or or_1 (or_1_out, and_2_out, and_1_out);
  nand nand_3 (nand_3_out, or_1_out, in_3);
  nand nand_4 (nand_4_out, in_3, not_1_out);
  not not_1 (not_1_out, or_1_out);
endmodule
